// Logisim project CRC.circ as structural Verilog: 2 circuits, main circuit CRC
module CRC (
  input  [7:0] A,
  input  [3:0] B,
  output [10:0] out_3
);

  wire [2:0] mod2_div_1_out_4, mod2_div_2_out_4, mod2_div_3_out_4, mod2_div_4_out_4, mod2_div_6_out_4,
       mod2_div_7_out_4;
  wire [3:1] mod2_div_5_out_4;

  mod2_div mod2_div_1 (.A(A[7:4]), .B(B), .out_4(mod2_div_1_out_4));  // open: D
  mod2_div mod2_div_2 (.A({mod2_div_1_out_4, A[3]}), .B(B), .out_4(mod2_div_2_out_4));  // open: D
  mod2_div mod2_div_3 (.A({mod2_div_2_out_4, A[2]}), .B(B), .out_4(mod2_div_3_out_4));  // open: D
  mod2_div mod2_div_4 (.A({mod2_div_3_out_4, A[1]}), .B(B), .out_4(mod2_div_4_out_4));  // open: D
  mod2_div mod2_div_5 (.A({mod2_div_4_out_4, A[0]}), .B(B), .out_4(mod2_div_5_out_4));  // open: D
  mod2_div mod2_div_6 (.A({mod2_div_5_out_4, 1'b0}), .B(B), .out_4(mod2_div_6_out_4));  // open: D
  mod2_div mod2_div_7 (.A({mod2_div_6_out_4, 1'b0}), .B(B), .out_4(mod2_div_7_out_4));  // open: D
  mod2_div mod2_div_8 (.A({mod2_div_7_out_4, 1'b0}), .B(B), .out_4(out_3[2:0]));  // open: D

  assign out_3[10:3] = A;
endmodule

module mod2_div (
  input  [3:0] A,
  input  [3:0] B,
  output D,
  output [2:0] out_4
);

  wire [3:0] xor_1_out;

  assign xor_1_out = A ^ B;  // XOR_Gate xor_1, 4 bits wide
  Multiplexer #(.width(3)) multiplexer_1 (.in0(A[2:0]), .in1(xor_1_out[2:0]), .out(out_4), .sel(A[3]));  // open: en

  assign D = A[3];
endmodule
