// Logisim project FSM.circ as structural Verilog: 3 circuits, main circuit fsm
module fsm (
  input  [1:0] in_1,
  input  clr,
  output out_3
);

  wire clock_1_out, register_1_q, register_2_q, register_3_q, state_tran_1_state0, state_tran_1_state1,
       state_tran_1_state2;

  state_tran state_tran_1 (
    .clr(clr), .state2_(register_1_q), .state1_(register_2_q), .state0_(register_3_q), .in1(in_1[1]),
    .in0(in_1[0]), .state2(state_tran_1_state2), .state1(state_tran_1_state1), .state0(state_tran_1_state0));
  Clock clock_1 (.out(clock_1_out));
  Register #(.width(1)) register_1 (.D(state_tran_1_state2), .Q(register_1_q), .clk(clock_1_out));  // open: en, clr
  Register #(.width(1)) register_2 (.D(state_tran_1_state1), .Q(register_2_q), .clk(clock_1_out));  // open: en, clr
  Register #(.width(1)) register_3 (.D(state_tran_1_state0), .Q(register_3_q), .clk(clock_1_out));  // open: en, clr
  Output output_1 (
    .state2(register_1_q), .state1(register_2_q), .state0(register_3_q), .in1(in_1[1]), .in0(in_1[0]),
    .Z(out_3));
endmodule

module state_tran (
  input  clr,
  input  state2_,
  input  state1_,
  input  state0_,
  input  in1,
  input  in0,
  output state2,
  output state1,
  output state0
);

  wire and_3_out, and_4_out, and_5_out, not_1_out, not_2_out, not_3_out, not_4_out, not_5_out, not_6_out,
       not_7_out, not_8_out, not_9_out, not_10_out, not_11_out, not_12_out, not_13_out, not_14_out;

  not not_1 (not_1_out, clr);
  not not_2 (not_2_out, state2_);
  not not_3 (not_3_out, in0);
  not not_4 (not_4_out, clr);
  not not_5 (not_5_out, state2_);
  not not_6 (not_6_out, in0);
  not not_7 (not_7_out, clr);
  not not_8 (not_8_out, in1);
  not not_9 (not_9_out, clr);
  not not_10 (not_10_out, state2_);
  not not_11 (not_11_out, in0);
  not not_12 (not_12_out, clr);
  not not_13 (not_13_out, state2_);
  not not_14 (not_14_out, in0);
  and and_1 (state2, not_1_out, not_2_out, state1_, not_3_out);
  and and_2 (state1, not_4_out, not_5_out, state0_, not_6_out);
  and and_3 (and_3_out, not_7_out, not_8_out, in0);
  and and_4 (and_4_out, not_9_out, not_10_out, state0_, in1, not_11_out);
  and and_5 (and_5_out, not_12_out, not_13_out, state1_, in1, not_14_out);
  or or_1 (state0, and_3_out, and_4_out, and_5_out);
endmodule

module Output (
  input  state2,
  input  state1,
  input  state0,
  input  in1,
  input  in0,
  output Z
);

  wire not_1_out, not_2_out;

  not not_1 (not_1_out, state2);
  not not_2 (not_2_out, in0);
  and and_1 (Z, not_1_out, state1, not_2_out);
endmodule
