// Logisim project GRF.circ as structural Verilog: 6 circuits, main circuit grf
module grf (
  input  [31:0] WD,
  input  [4:0] A3_write_in,
  input  clk,
  input  reset,
  input  WE,
  input  [4:0] A1_output_slt,
  input  [4:0] A2_output_slt,
  output [31:0] RD1,
  output [31:0] RD2
);

  wire _0_3write, _4_7write, _8_11write, _12_15write, _16_19write, _20_23write, _24_27write, _28_31write;
  wire [1:0] _0_3op1, _0_3op2, _0_3write_slt, _4_7op1, _4_7op2, _4_7write_slt, _8_11op1, _8_11op2,
       _8_11write_slt, _12_15op1, _12_15op2, _12_15write_slt, _16_19op1, _16_19op2, _16_19write_slt,
       _20_23op1, _20_23op2, _20_23write_slt, _24_27op1, _24_27op2, _24_27write_slt, _28_31op1, _28_31op2,
       _28_31write_slt, selector_1_output_low2;
  wire [2:0] selector_1_output_high3;
  wire [31:0] _0_3_output1, _0_3_output2, _4_7_out_10, _4_7_output1, _8_11_out_10, _8_11_output1,
       _12_15_out_10, _12_15_output1, _16_19_out_10, _16_19_output1, _20_23_out_10, _20_23_output1,
       _24_27_out_10, _24_27_output1, _28_31_out_10, _28_31_output1;

  selector selector_1 (
    .in_1(A3_write_in), .output_low2(selector_1_output_low2), .output_high3(selector_1_output_high3));
  selector_2 selector_2 (
    .in_1(A1_output_slt), .out_2(_0_3op1), .out_3(_4_7op1), .out_4(_8_11op1), .out_5(_12_15op1),
    .out_6(_16_19op1), .out_7(_20_23op1), .out_8(_24_27op1), .out_9(_28_31op1));
  Demultiplexer #(.select(3), .width(2)) demultiplexer_1 (
    .out0(_0_3write_slt), .out1(_4_7write_slt), .out2(_8_11write_slt), .out3(_12_15write_slt),
    .out4(_16_19write_slt), .out5(_20_23write_slt), .out6(_24_27write_slt), .out7(_28_31write_slt),
    .in(selector_1_output_low2), .sel(selector_1_output_high3));  // open: en
  Decoder #(.select(3)) decoder_1 (
    .out0(_0_3write), .out1(_4_7write), .out2(_8_11write), .out3(_12_15write), .out4(_16_19write),
    .out5(_20_23write), .out6(_24_27write), .out7(_28_31write), .sel(selector_1_output_high3));  // open: en
  selector_2 selector_3 (
    .in_1(A2_output_slt), .out_2(_0_3op2), .out_3(_4_7op2), .out_4(_8_11op2), .out_5(_12_15op2),
    .out_6(_16_19op2), .out_7(_20_23op2), .out_8(_24_27op2), .out_9(_28_31op2));
  reg0_3 _0_3 (
    .write_in(WD), .write_in_select(_0_3write_slt), .output_select1(_0_3op1), .reset(reset), .clk(clk),
    .WE(WE), .output1(_0_3_output1), .en(_0_3write), .output_select2(_0_3op2), .output2(_0_3_output2));
  \reg  _4_7 (
    .write_in(WD), .write_in_select(_4_7write_slt), .output_select1(_4_7op1), .reset(reset), .clk(clk),
    .WE(WE), .output1(_4_7_output1), .en(_4_7write), .output_select2(_4_7op2), .out_10(_4_7_out_10));
  \reg  _8_11 (
    .write_in(WD), .write_in_select(_8_11write_slt), .output_select1(_8_11op1), .reset(reset), .clk(clk),
    .WE(WE), .output1(_8_11_output1), .en(_8_11write), .output_select2(_8_11op2), .out_10(_8_11_out_10));
  \reg  _12_15 (
    .write_in(WD), .write_in_select(_12_15write_slt), .output_select1(_12_15op1), .reset(reset), .clk(clk),
    .WE(WE), .output1(_12_15_output1), .en(_12_15write), .output_select2(_12_15op2), .out_10(_12_15_out_10));
  \reg  _16_19 (
    .write_in(WD), .write_in_select(_16_19write_slt), .output_select1(_16_19op1), .reset(reset), .clk(clk),
    .WE(WE), .output1(_16_19_output1), .en(_16_19write), .output_select2(_16_19op2), .out_10(_16_19_out_10));
  \reg  _20_23 (
    .write_in(WD), .write_in_select(_20_23write_slt), .output_select1(_20_23op1), .reset(reset), .clk(clk),
    .WE(WE), .output1(_20_23_output1), .en(_20_23write), .output_select2(_20_23op2), .out_10(_20_23_out_10));
  \reg  _24_27 (
    .write_in(WD), .write_in_select(_24_27write_slt), .output_select1(_24_27op1), .reset(reset), .clk(clk),
    .WE(WE), .output1(_24_27_output1), .en(_24_27write), .output_select2(_24_27op2), .out_10(_24_27_out_10));
  \reg  _28_31 (
    .write_in(WD), .write_in_select(_28_31write_slt), .output_select1(_28_31op1), .reset(reset), .clk(clk),
    .WE(WE), .output1(_28_31_output1), .en(_28_31write), .output_select2(_28_31op2), .out_10(_28_31_out_10));
  Multiplexer #(.select(3), .width(32)) multiplexer_1 (
    .in0(_0_3_output1), .in1(_4_7_output1), .in2(_8_11_output1), .in3(_12_15_output1), .in4(_16_19_output1),
    .in5(_20_23_output1), .in6(_24_27_output1), .in7(_28_31_output1), .out(RD1), .sel(A1_output_slt[4:2]));  // open: en
  Multiplexer #(.select(3), .width(32)) multiplexer_2 (
    .in0(_0_3_output2), .in1(_4_7_out_10), .in2(_8_11_out_10), .in3(_12_15_out_10), .in4(_16_19_out_10),
    .in5(_20_23_out_10), .in6(_24_27_out_10), .in7(_28_31_out_10), .out(RD2), .sel(A2_output_slt[4:2]));  // open: en

  // Other names for the same wires on the sheet: select1[2:0] = A1_output_slt[4:2]; select2[2:0] = A2_output_slt[4:2]
endmodule

module reg0_3 (
  input  [31:0] write_in,
  input  [1:0] write_in_select,
  input  en,
  input  [1:0] output_select1,
  input  reset,
  input  clk,
  input  WE,
  input  [1:0] output_select2,
  output [31:0] output1,
  output [31:0] output2
);

  wire decoder_1_out1, decoder_1_out2, decoder_1_out3;
  wire [31:0] _0_q, _1_q, _2_q, _3_q, demultiplexer_1_out1, demultiplexer_1_out2, demultiplexer_1_out3,
       multiplexer_1_out, multiplexer_2_out, multiplexer_3_out;

  Demultiplexer #(.select(2), .width(32)) demultiplexer_1 (
    .out1(demultiplexer_1_out1), .out2(demultiplexer_1_out2), .out3(demultiplexer_1_out3), .in(write_in),
    .sel(write_in_select));  // open: out0, en
  Decoder #(.select(2), .disabled(0)) decoder_1 (
    .out1(decoder_1_out1), .out2(decoder_1_out2), .out3(decoder_1_out3), .sel(write_in_select), .en(en));  // open: out0
  Multiplexer #(.width(32)) multiplexer_1 (
    .in0(_1_q), .in1(demultiplexer_1_out1), .out(multiplexer_1_out), .sel(decoder_1_out1));  // open: en
  Multiplexer #(.width(32)) multiplexer_2 (
    .in0(_2_q), .in1(demultiplexer_1_out2), .out(multiplexer_2_out), .sel(decoder_1_out2));  // open: en
  Multiplexer #(.width(32)) multiplexer_3 (
    .in0(_3_q), .in1(demultiplexer_1_out3), .out(multiplexer_3_out), .sel(decoder_1_out3));  // open: en
  Register #(.width(32)) _0 (.D({32{1'b0}}), .en(WE), .Q(_0_q), .clk(clk), .clr(reset));
  Register #(.width(32)) _1 (.D(multiplexer_1_out), .en(WE), .Q(_1_q), .clk(clk), .clr(reset));
  Register #(.width(32)) _2 (.D(multiplexer_2_out), .en(WE), .Q(_2_q), .clk(clk), .clr(reset));
  Register #(.width(32)) _3 (.D(multiplexer_3_out), .en(WE), .Q(_3_q), .clk(clk), .clr(reset));
  Multiplexer #(.select(2), .width(32)) multiplexer_4 (
    .in0(_0_q), .in1(_1_q), .in2(_2_q), .in3(_3_q), .out(output1), .sel(output_select1));  // open: en
  Multiplexer #(.select(2), .width(32)) multiplexer_5 (
    .in0(_0_q), .in1(_1_q), .in2(_2_q), .in3(_3_q), .out(output2), .sel(output_select2));  // open: en
endmodule

// output2
module \reg  (
  input  [31:0] write_in,
  input  [1:0] write_in_select,
  input  en,
  input  [1:0] output_select1,
  input  [1:0] output_select2,
  input  reset,
  input  clk,
  input  WE,
  output [31:0] output1,
  output [31:0] out_10
);

  wire decoder_1_out0, decoder_1_out1, decoder_1_out2, decoder_1_out3;
  wire [31:0] _1_2_q, _1_q, _2_q, _3_q, demultiplexer_1_out0, demultiplexer_1_out1, demultiplexer_1_out2,
       demultiplexer_1_out3, multiplexer_1_out, multiplexer_2_out, multiplexer_3_out, multiplexer_4_out;

  Demultiplexer #(.select(2), .width(32)) demultiplexer_1 (
    .out0(demultiplexer_1_out0), .out1(demultiplexer_1_out1), .out2(demultiplexer_1_out2),
    .out3(demultiplexer_1_out3), .in(write_in), .sel(write_in_select));  // open: en
  Decoder #(.select(2), .disabled(0)) decoder_1 (
    .out0(decoder_1_out0), .out1(decoder_1_out1), .out2(decoder_1_out2), .out3(decoder_1_out3),
    .sel(write_in_select), .en(en));
  Multiplexer #(.width(32)) multiplexer_1 (
    .in0(_1_q), .in1(demultiplexer_1_out0), .out(multiplexer_1_out), .sel(decoder_1_out0));  // open: en
  Multiplexer #(.width(32)) multiplexer_2 (
    .in0(_1_2_q), .in1(demultiplexer_1_out1), .out(multiplexer_2_out), .sel(decoder_1_out1));  // open: en
  Multiplexer #(.width(32)) multiplexer_3 (
    .in0(_2_q), .in1(demultiplexer_1_out2), .out(multiplexer_3_out), .sel(decoder_1_out2));  // open: en
  Multiplexer #(.width(32)) multiplexer_4 (
    .in0(_3_q), .in1(demultiplexer_1_out3), .out(multiplexer_4_out), .sel(decoder_1_out3));  // open: en
  Register #(.width(32)) _1 (.D(multiplexer_1_out), .en(WE), .Q(_1_q), .clk(clk), .clr(reset));
  Register #(.width(32)) _1_2 (.D(multiplexer_2_out), .en(WE), .Q(_1_2_q), .clk(clk), .clr(reset));
  Register #(.width(32)) _2 (.D(multiplexer_3_out), .en(WE), .Q(_2_q), .clk(clk), .clr(reset));
  Register #(.width(32)) _3 (.D(multiplexer_4_out), .en(WE), .Q(_3_q), .clk(clk), .clr(reset));
  Multiplexer #(.select(2), .width(32)) multiplexer_5 (
    .in0(_1_q), .in1(_1_2_q), .in2(_2_q), .in3(_3_q), .out(output1), .sel(output_select1));  // open: en
  Multiplexer #(.select(2), .width(32)) multiplexer_6 (
    .in0(_1_q), .in1(_1_2_q), .in2(_2_q), .in3(_3_q), .out(out_10), .sel(output_select2));  // open: en
endmodule

module selector (
  input  [4:0] in_1,
  output [1:0] output_low2,
  output [2:0] output_high3
);


  assign output_high3 = in_1[4:2];
  assign output_low2 = in_1[1:0];
endmodule

module selector_2 (
  input  [4:0] in_1,
  output [1:0] out_2,
  output [1:0] out_3,
  output [1:0] out_4,
  output [1:0] out_5,
  output [1:0] out_6,
  output [1:0] out_7,
  output [1:0] out_8,
  output [1:0] out_9
);

  wire [1:0] selector_1_output_low2;
  wire [2:0] selector_1_output_high3;

  selector selector_1 (.in_1(in_1), .output_low2(selector_1_output_low2), .output_high3(selector_1_output_high3));
  Demultiplexer #(.select(3), .width(2)) demultiplexer_1 (
    .out0(out_2), .out1(out_3), .out2(out_4), .out3(out_5), .out4(out_6), .out5(out_7), .out6(out_8),
    .out7(out_9), .in(selector_1_output_low2), .sel(selector_1_output_high3));  // open: en
endmodule

module text (
  input  WE,
  input  reset,
  input  clk,
  input  [4:0] A1,
  input  [4:0] A2,
  input  [4:0] A3,
  input  [31:0] in_7,
  output [31:0] out_8,
  output [31:0] out_9
);

  grf grf_1 (
    .WD(in_7), .A3_write_in(A3), .clk(clk), .reset(reset), .WE(WE), .A1_output_slt(A1), .A2_output_slt(A2),
    .RD1(out_8), .RD2(out_9));
endmodule
