// Logisim project ftoi.circ as structural Verilog: 2 circuits, main circuit ftoi
module ftoi (
  input  [15:0] in_1,
  output [31:0] out_2
);

  wire [2:0] comparator_1_lt, comparator_2_gt;
  wire [4:0] subtractor_1_out, subtractor_2_out, subtractor_3_out;
  wire [30:0] shifter_1_out;
  wire [31:0] div_1_out_3, div_2_out_3, div_3_out_3, multiplexer_1_out, multiplexer_2_out, shifter_2_out;

  // Probe on in_1[14:10]
  Subtractor #(.width(5)) subtractor_1 (.a(in_1[14:10]), .b(5'b01111), .out(subtractor_1_out));  // open: bin, bout
  // Probe on subtractor_1_out
  Comparator #(.width(5)) comparator_1 (
    .a(subtractor_1_out), .b({5{1'b0}}), .gt(comparator_1_lt[2]), .eq(comparator_1_lt[1]),
    .lt(comparator_1_lt[0]));
  Comparator #(.width(5)) comparator_2 (
    .a(subtractor_1_out), .b(5'b01010), .gt(comparator_2_gt[0]), .eq(comparator_2_gt[1]),
    .lt(comparator_2_gt[2]));
  Subtractor #(.width(5)) subtractor_2 (.a(5'b01010), .b(subtractor_1_out), .out(subtractor_2_out));  // open: bin, bout
  Shifter #(.width(31), .shift("lr")) shifter_1 (
    .in({21'h1, in_1[9:0]}), .\dist (subtractor_2_out), .out(shifter_1_out));
  Subtractor #(.width(5)) subtractor_3 (
    .a({5{1'b1}}), .b(subtractor_1_out), .out(subtractor_3_out));  // open: bin, bout
  div div_1 (.in_1(shifter_1_out), .in_2(in_1[15]), .out_3(div_1_out_3));
  Shifter #(.width(32), .shift("lr")) shifter_2 (
    .in({1'b1, in_1[9:0], {21{1'b0}}}), .\dist (subtractor_3_out), .out(shifter_2_out));
  div div_2 (.in_1(shifter_2_out[30:0]), .in_2(in_1[15]), .out_3(div_2_out_3));
  div div_3 (.in_1({21'h1, in_1[9:0]}), .in_2(in_1[15]), .out_3(div_3_out_3));
  Multiplexer #(.width(32)) multiplexer_1 (
    .in0(32'h1), .in1({32{1'b1}}), .out(multiplexer_1_out), .sel(in_1[15]));  // open: en
  Multiplexer #(.select(3), .width(32), .disabled(0), .enable("false")) multiplexer_2 (
    .in1(div_2_out_3), .in2(div_3_out_3), .in4(div_1_out_3), .out(multiplexer_2_out), .sel(comparator_2_gt));  // open: in0, in3, in5, in6, in7
  Multiplexer #(.select(3), .width(32), .disabled(0), .enable("false")) multiplexer_3 (
    .in1({32{1'b0}}), .in2(multiplexer_1_out), .in4(multiplexer_2_out), .out(out_2), .sel(comparator_1_lt));  // open: in0, in3, in5, in6, in7
endmodule

module div (
  input  [30:0] in_1,
  input  in_2,
  output [31:0] out_3
);

  wire [31:0] adder_1_out, not_1_out;

  // Probe on not_1_out
  assign not_1_out = ~{1'b0, in_1};  // NOT_Gate not_1, 32 bits wide
  Multiplexer #(.width(32)) multiplexer_1 (.in0({1'b0, in_1}), .in1(adder_1_out), .out(out_3), .sel(in_2));  // open: en
  Adder #(.width(32)) adder_1 (.a(not_1_out), .b(32'h1), .out(adder_1_out));  // open: cin, cout
endmodule
