// Logisim project navigation.circ as structural Verilog: 4 circuits, main circuit navigation
module navigation (
  input  [1:0] dir,
  input  clk,
  input  reset,
  output arrive,
  output out_5
);

  wire register_1_q, register_2_q, register_3_q, state_transition_1_state0, state_transition_1_state1,
       state_transition_1_state2;

  state_transition state_transition_1 (
    .state2_(register_1_q), .state1_(register_2_q), .state0_(register_3_q), .dir1(dir[1]), .dir0(dir[0]),
    .state2(state_transition_1_state2), .state1(state_transition_1_state1), .state0(state_transition_1_state0));
  Register #(.width(1)) register_1 (
    .D(state_transition_1_state2), .Q(register_1_q), .clk(clk), .clr(reset));  // open: en
  Register #(.width(1)) register_2 (
    .D(state_transition_1_state1), .Q(register_2_q), .clk(clk), .clr(reset));  // open: en
  Register #(.width(1)) register_3 (
    .D(state_transition_1_state0), .Q(register_3_q), .clk(clk), .clr(reset));  // open: en
  Output output_1 (.state2(register_1_q), .state1(register_2_q), .state0(register_3_q), .arrive(arrive));
  output_hit output_hit_1 (
    .state2(register_1_q), .state1(register_2_q), .state0(register_3_q), .dir1(dir[1]), .dir0(dir[0]),
    .clk(clk), .reset(reset), .hit(out_5));
endmodule

module state_transition (
  input  state2_,
  input  state1_,
  input  state0_,
  input  dir1,
  input  dir0,
  output state2,
  output state1,
  output state0
);

  wire and_1_out, and_2_out, and_3_out, and_4_out, and_5_out, and_6_out, and_7_out, and_8_out, and_9_out,
       and_10_out, and_11_out, not_1_out, not_2_out, not_3_out, not_4_out, not_5_out, not_6_out, not_7_out,
       not_8_out, not_9_out, not_10_out, not_11_out, not_12_out, not_13_out, not_14_out, not_15_out,
       not_16_out, not_17_out, not_18_out, not_19_out, not_20_out, not_21_out, not_22_out, not_23_out,
       not_24_out, not_25_out, not_26_out, not_27_out;

  not not_1 (not_1_out, state2_);
  not not_2 (not_2_out, state0_);
  not not_3 (not_3_out, dir1);
  not not_4 (not_4_out, dir0);
  not not_5 (not_5_out, state2_);
  not not_6 (not_6_out, dir1);
  not not_7 (not_7_out, state2_);
  not not_8 (not_8_out, state1_);
  not not_9 (not_9_out, dir1);
  not not_10 (not_10_out, state2_);
  not not_11 (not_11_out, dir1);
  not not_12 (not_12_out, dir0);
  not not_13 (not_13_out, state2_);
  not not_14 (not_14_out, state0_);
  not not_15 (not_15_out, dir1);
  not not_16 (not_16_out, state2_);
  not not_17 (not_17_out, state0_);
  not not_18 (not_18_out, dir0);
  not not_19 (not_19_out, state2_);
  not not_20 (not_20_out, state2_);
  not not_21 (not_21_out, state1_);
  not not_22 (not_22_out, dir1);
  not not_23 (not_23_out, dir0);
  not not_24 (not_24_out, state2_);
  not not_25 (not_25_out, state2_);
  not not_26 (not_26_out, state2_);
  not not_27 (not_27_out, dir0);
  and and_1 (and_1_out, not_1_out, state1_, not_2_out, not_3_out, not_4_out);
  and and_2 (and_2_out, not_5_out, state1_, state0_, not_6_out, dir0);
  and and_3 (and_3_out, not_7_out, not_8_out, state0_, not_9_out);
  and and_4 (and_4_out, not_10_out, state0_, not_11_out, not_12_out);
  and and_5 (and_5_out, not_13_out, state1_, not_14_out, not_15_out, dir0);
  and and_6 (and_6_out, not_16_out, state1_, not_17_out, dir1, not_18_out);
  and and_7 (and_7_out, not_19_out, state1_, state0_, dir1, dir0);
  and and_8 (and_8_out, not_20_out, not_21_out, not_22_out, not_23_out);
  and and_9 (and_9_out, not_24_out, state0_, dir1, dir0);
  and and_10 (and_10_out, not_25_out, state1_, dir1, dir0);
  and and_11 (and_11_out, not_26_out, state1_, state0_, not_27_out);
  or or_1 (state2, and_1_out, and_2_out);
  or or_2 (state1, and_3_out, and_4_out, and_5_out, and_6_out, and_7_out);
  or or_3 (state0, and_8_out, and_9_out, and_10_out, and_11_out);
endmodule

module Output (
  input  state2,
  input  state1,
  input  state0,
  output arrive
);

  wire not_1_out, not_2_out;

  not not_1 (not_1_out, state1);
  not not_2 (not_2_out, state0);
  and and_1 (arrive, state2, not_1_out, not_2_out);
endmodule

module output_hit (
  input  state2,
  input  state1,
  input  state0,
  input  dir1,
  input  dir0,
  input  clk,
  input  reset,
  output hit
);

  wire and_1_out, and_2_out, and_3_out, and_4_out, and_5_out, not_1_out, not_2_out, not_3_out, not_4_out,
       not_5_out, not_6_out, not_7_out, not_8_out, not_9_out, not_10_out, not_11_out, not_12_out, or_1_out;

  not not_1 (not_1_out, state2);
  not not_2 (not_2_out, state0);
  not not_3 (not_3_out, dir1);
  not not_4 (not_4_out, state2);
  not not_5 (not_5_out, state0);
  not not_6 (not_6_out, dir0);
  not not_7 (not_7_out, state2);
  not not_8 (not_8_out, state1);
  not not_9 (not_9_out, state2);
  not not_10 (not_10_out, state2);
  not not_11 (not_11_out, dir1);
  not not_12 (not_12_out, dir0);
  and and_1 (and_1_out, not_1_out, not_2_out, not_3_out, dir0);
  and and_2 (and_2_out, not_4_out, not_5_out, dir1, not_6_out);
  and and_3 (and_3_out, not_7_out, not_8_out, dir1, dir0);
  and and_4 (and_4_out, not_9_out, state0, dir1, dir0);
  and and_5 (and_5_out, not_10_out, state1, state0, not_11_out, not_12_out);
  or or_1 (or_1_out, and_1_out, and_2_out, and_3_out, and_4_out, and_5_out);
  Register #(.width(1)) register_1 (.D(or_1_out), .Q(hit), .clk(clk), .clr(reset));  // open: en
endmodule
