// Logisim project 单周期CPU.circ as structural Verilog: 14 circuits, main circuit main
module main (
  input  in_1,
  output [31:0] out_2,
  output [31:0] out_3,
  output out_4,
  output [4:0] out_5,
  output [31:0] out_6,
  output out_7,
  output [31:0] out_8,
  output [31:0] out_9
);

  wire alu_1_zero, clk, comparator_1_eq, controller_1_alubsel, controller_1_extop, controller_1_sllop;
  wire [1:0] alu_1_out_4, controller_1_dmop, controller_1_wdsel, controller_1_wra3sel;
  wire [2:0] controller_1_aluop, controller_1_npcop;
  wire [31:0] adder_1_out, dm_1_rd, ext_1_extend, grf_1_rd1, grf_1_rd2, multiplexer_4_out, multiplexer_5_out,
       npc_1_npc, npc_1_pc_4, register_1_q, subtractor_1_out;

  Comparator #(.width(32)) comparator_1 (.a({32{1'b0}}), .b(register_1_q), .eq(comparator_1_eq));  // open: gt, lt
  Register #(.width(32)) register_1 (.D(npc_1_npc), .Q(register_1_q), .clk(clk), .clr(in_1));  // open: en
  Adder #(.width(32)) adder_1 (.a(register_1_q), .b(32'h3000), .out(adder_1_out));  // open: cin, cout
  Clock clock_1 (.out(clk));
  Multiplexer #(.width(32)) multiplexer_1 (
    .in0(register_1_q), .in1(adder_1_out), .out(out_3), .sel(comparator_1_eq));  // open: en
  NPC npc_1 (
    .PC(out_3), .IMM(out_2[25:0]), .Zero(alu_1_zero), .NPCOp(controller_1_npcop), .RA(grf_1_rd1),
    .PC_4(npc_1_pc_4), .NPC(npc_1_npc));
  Subtractor #(.width(32)) subtractor_1 (.a(out_3), .b(32'h3000), .out(subtractor_1_out));  // open: bin, bout
  ROM #(.addrWidth(16), .dataWidth(32)) rom_1 (.addr(subtractor_1_out[17:2]), .data(out_2));  // open: sel
  Multiplexer #(.select(2), .width(32)) multiplexer_2 (
    .in0(dm_1_rd), .in1({out_8[31:2], alu_1_out_4}), .in2(npc_1_pc_4), .out(out_6), .sel(controller_1_wdsel));  // open: in3, en
  Multiplexer #(.select(2), .width(5)) multiplexer_3 (
    .in0(out_2[15:11]), .in1(out_2[20:16]), .in2({5{1'b1}}), .out(out_5), .sel(controller_1_wra3sel));  // open: in3, en
  Controller controller_1 (
    .opcode(out_2[31:26]), .func(out_2[5:0]), .EXTOp(controller_1_extop), .WE(out_4),
    .ALUBSel(controller_1_alubsel), .ALUOp(controller_1_aluop), .DMWr(out_7), .DMOp(controller_1_dmop),
    .NPCOp(controller_1_npcop), .sllOp(controller_1_sllop), .WRA3Sel(controller_1_wra3sel),
    .WDSel(controller_1_wdsel));
  GRF grf_1 (
    .WD(out_6), .A3_write_in(out_5), .clk(clk), .reset(in_1), .WE(out_4), .A1_output_slt(out_2[25:21]),
    .A2_output_slt(out_2[20:16]), .RD1(grf_1_rd1), .RD2(grf_1_rd2));
  Multiplexer #(.width(32)) multiplexer_4 (
    .in0(grf_1_rd1), .in1(grf_1_rd2), .out(multiplexer_4_out), .sel(controller_1_sllop));  // open: en
  Ext ext_1 (.IMM_15_0(out_2[15:0]), .extend(ext_1_extend), .EXTOp(controller_1_extop));
  Multiplexer #(.width(32)) multiplexer_5 (
    .in0(grf_1_rd2), .in1(ext_1_extend), .out(multiplexer_5_out), .sel(controller_1_alubsel));  // open: en
  ALU alu_1 (
    .A(multiplexer_4_out), .B(multiplexer_5_out), .in_3(controller_1_aluop),
    .out_4({out_8[31:2], alu_1_out_4}), .Zero(alu_1_zero));  // open: LessZero
  DM dm_1 (
    .Addr({out_8[31:2], alu_1_out_4}), .WD(grf_1_rd2), .clk(clk), .reset(in_1), .DMWr(out_7), .RD(dm_1_rd),
    .DMOp(controller_1_dmop), .out_7(out_9));

  assign out_8[1:0] = 2'b00;

  // Other names for the same wires on the sheet: Instr[31:0] = out_2; MemAddr[31:2] = out_8[31:2];
  //   MemData[31:0] = out_9; MemWrite = out_7; pc[31:0] = out_3; RegAddr[4:0] = out_5; RegData[31:0] = out_6;
  //   RegWrite = out_4; reset = in_1

  // Notes on the sheet:
  //   PC
  //   IM
  //   contents of rom_1 (hex, n*v repeats v):
  //   8d480000 8000c02 3c03430d 3c100000 8e06000c 3c050000 a0b80000 3c0814d5 34e0da4c 8000c0a 8000c0e
  //   12e50000 1002809 34d27083 3c030000 ac6c0000 ae20000c 274c820 3c0e0000 adcd0010 35f57d7b 2103822
  //   11d70000 3c040000 ac950000 2508022 3c1387b1 180a40 10870003 3c030000 806f000c 36a51e6f 3c01f214
  //   81d4000c 8b9020 8000c24 3c10bb58 0 3c040000 80930010 0 127a00 11630002 3c100000 8e090004 113b822
  //   2f8b820 81ee0004 12d80001 81cc0008 3c11f6c2 aac80 8000c39 e00008 c000c37 aef90000 1200008 22a022
  //   af310010 c000c46 c000c3d 81e80000 c000c44 12050000 3c040000 8c8e0004 14940 8d78000c 34c76a6c 0
  //   1c97820 1591020 107fc0 10070009 3001809 c000c4f 8000c4e c22c0 aef50000 362b0021 2f91820 a5000 8d0820
  //   3c070000 8cf60000 3c020000 ac570010 c000c58 2a08020 12700004 3c020000 a054000c 3c070000 80e30010
  //   3c16fe7e 34a53ab3 3c130000 8e630010 3c10497b 1f66020 49640 3c130000 826f0008 152040 3c0d0000
  //   a1a3000c 0 0 8000c6d c00022 3c08862b 2234020 3c150000 82b6000c 3c020000 a0490000 302c0 c000c76
  //   3c18b043 8000c79 147800 3c088281 12280 3c0c0000 ad890004 131540 1660c0 3c170000 a2f90008 3c020000
  //   ac470004 12100 8000c86 528820 0 3c000000 ac110000 11cb0003 3c110000 36310032 1188c0 3c040000
  //   8c990010 c000c91 b1740 c000c92 1728822 211c0 0 3c170000 a2f90010 0 100f0001 3c008fa6 c000c9d 2278820
  //   ace20004 aee70010 0 8000ca0 8000ca1 0 0 0 c000ca6 36f5182a 10920006 35c868ee 82ce000c 3c1023a0
  //   8000cab 36349ab0 a2d70000 a9022 3c010000 8c2d0008 c000cb5 12d10000 2400008 8000cb4 8dd00008 10b90009
  //   3667824d 36637def 3c090000 35290001 3c080000 3c140000 35080064 36940032 c000cbf 11140002 289a020
  //   3e00008 3c1473b9 3c140000 a2870000 8c310008 c000cc7 81580010 0 3658cf49 11080000 11f80000 2982020
  //   10480003 12ca0001 8d370008 3c16b14a 8000cd3 273a022 c18022 d9000 8000cd6 a02d0000 0 0 c000cda
  //   1309822 0 3c082658 0 3109822 30d4822 0 3c080000 ad05000c 3188822 d47020 0 3c160000 aec40010 0
  //   35598317 35f648fe aef10010 3c080000 8d110000 11010000 a1180008 3587628a 152c0 0 0 34769ebc 3c170000
  //   a2e80008 6a5020 3c190000 a3320004 3c17ed40 2aba022 3c050000 80ad0010 8000cff 3c13438c 1b12020
  //   8000d02 1c4a022 11c60000 1434022 3c06459f a0eb000c 3c130000 8e720010 3c0f3ba8 c000d0c 0 8d0c0010
  //   175b020 241c0 3c0c0000 a18a000c 3c100000 a2130004 ac4b0000 3c040000 3c170000 82ee0000 3c100000
  //   a2050008 3c080000 8d160010 321022 38c820 2ed9022 c000d21 3c040000 a0930010 3c090000 81380000
  //   3c09f0c1 340b5786 a2f8000c 3c020000 804a0000 a1730000 3c070000 ace70000 12ea0002 3c0d0000 8da40008
  //   ea7822 c23022 0 3c0c0000 81840008 c000d37 8000d35 d4ec0 36b3ef02 c000d38 3c000000 ac070004 3c050000
  //   8cb2000c 0 1659822 34b3bce1 d90c0 d9000 3c170000 aef90010 18f80 30bc020 80400004 e7c00 eb040 c000d4b
  //   177e80 2d78022 3c1888d1 351386d1 128c0000 822b0004 3c140000 36940014 82900008 c000d55 3c0d0000
  //   8dac0000 3c0e04a3 3c153b54 f24c0 11630000 88f00 b81020 3c180000 af150028 f1980 8000d60 36302613
  //   ade4000c 3c0ca7d8 0 da6c0 c000d65 8d500010 3c020000 80500004 8000d69 985c0 8d760000 11250000
  //   3c0995fc c000d6e 103400 597020 8242000c 8c620000 0 0 3c050000 a0b70008 3c100000 a2130004 30e7022
  //   8e0a000c 1485820 80540008 2568820 1354c0 a3180008 11a20001 195780 3c030000 806a0004 3c0d0000
  //   ada1000c 80550000 8000d87 34737e14 0 3c0a0000 354a002c 8d530010 12800000 196140 a218000c 1309022
  //   110e0000 a2b50008 c000d93 32e3022 3470aa3e ae910008 12d10000 3286822 ae360008 3c080000 3c100000
  //   36101187 ad100000 ad100050 361027ff ad100010 a1100003 2108020 ad100028 35080030 4*2088022 ad10fff0
  //   ad100100 36100046 a1100080 a1100400 810b0101
  //   addr $rs
  //   addr $rt
  //   addr $rd
endmodule

module GRF (
  input  [31:0] WD,
  input  [4:0] A3_write_in,
  input  clk,
  input  reset,
  input  WE,
  input  [4:0] A1_output_slt,
  input  [4:0] A2_output_slt,
  output [31:0] RD1,
  output [31:0] RD2
);

  wire _0_3write, _4_7write, _8_11write, _12_15write, _16_19write, _20_23write, _24_27write, _28_31write;
  wire [1:0] _0_3op1, _0_3op2, _0_3write_slt, _4_7op1, _4_7op2, _4_7write_slt, _8_11op1, _8_11op2,
       _8_11write_slt, _12_15op1, _12_15op2, _12_15write_slt, _16_19op1, _16_19op2, _16_19write_slt,
       _20_23op1, _20_23op2, _20_23write_slt, _24_27op1, _24_27op2, _24_27write_slt, _28_31op1, _28_31op2,
       _28_31write_slt, grf_selector_1_output_low2;
  wire [2:0] grf_selector_1_output_high3;
  wire [31:0] _0_3_output1, _0_3_output2, _4_7_out_10, _4_7_output1, _8_11_out_10, _8_11_output1,
       _12_15_out_10, _12_15_output1, _16_19_out_10, _16_19_output1, _20_23_out_10, _20_23_output1,
       _24_27_out_10, _24_27_output1, _28_31_out_10, _28_31_output1;

  GRF_selector grf_selector_1 (
    .in_1(A3_write_in), .output_low2(grf_selector_1_output_low2), .output_high3(grf_selector_1_output_high3));
  GRF_selector_2 grf_selector_2 (
    .in_1(A1_output_slt), .out_2(_0_3op1), .out_3(_4_7op1), .out_4(_8_11op1), .out_5(_12_15op1),
    .out_6(_16_19op1), .out_7(_20_23op1), .out_8(_24_27op1), .out_9(_28_31op1));
  Demultiplexer #(.select(3), .width(2)) demultiplexer_1 (
    .out0(_0_3write_slt), .out1(_4_7write_slt), .out2(_8_11write_slt), .out3(_12_15write_slt),
    .out4(_16_19write_slt), .out5(_20_23write_slt), .out6(_24_27write_slt), .out7(_28_31write_slt),
    .in(grf_selector_1_output_low2), .sel(grf_selector_1_output_high3));  // open: en
  Decoder #(.select(3)) decoder_1 (
    .out0(_0_3write), .out1(_4_7write), .out2(_8_11write), .out3(_12_15write), .out4(_16_19write),
    .out5(_20_23write), .out6(_24_27write), .out7(_28_31write), .sel(grf_selector_1_output_high3));  // open: en
  GRF_selector_2 grf_selector_3 (
    .in_1(A2_output_slt), .out_2(_0_3op2), .out_3(_4_7op2), .out_4(_8_11op2), .out_5(_12_15op2),
    .out_6(_16_19op2), .out_7(_20_23op2), .out_8(_24_27op2), .out_9(_28_31op2));
  GRF_reg0_3 _0_3 (
    .write_in(WD), .write_in_select(_0_3write_slt), .output_select1(_0_3op1), .reset(reset), .clk(clk),
    .WE(WE), .output1(_0_3_output1), .en(_0_3write), .output_select2(_0_3op2), .output2(_0_3_output2));
  GRF_reg _4_7 (
    .write_in(WD), .write_in_select(_4_7write_slt), .output_select1(_4_7op1), .reset(reset), .clk(clk),
    .WE(WE), .output1(_4_7_output1), .en(_4_7write), .output_select2(_4_7op2), .out_10(_4_7_out_10));
  GRF_reg _8_11 (
    .write_in(WD), .write_in_select(_8_11write_slt), .output_select1(_8_11op1), .reset(reset), .clk(clk),
    .WE(WE), .output1(_8_11_output1), .en(_8_11write), .output_select2(_8_11op2), .out_10(_8_11_out_10));
  GRF_reg _12_15 (
    .write_in(WD), .write_in_select(_12_15write_slt), .output_select1(_12_15op1), .reset(reset), .clk(clk),
    .WE(WE), .output1(_12_15_output1), .en(_12_15write), .output_select2(_12_15op2), .out_10(_12_15_out_10));
  GRF_reg _16_19 (
    .write_in(WD), .write_in_select(_16_19write_slt), .output_select1(_16_19op1), .reset(reset), .clk(clk),
    .WE(WE), .output1(_16_19_output1), .en(_16_19write), .output_select2(_16_19op2), .out_10(_16_19_out_10));
  GRF_reg _20_23 (
    .write_in(WD), .write_in_select(_20_23write_slt), .output_select1(_20_23op1), .reset(reset), .clk(clk),
    .WE(WE), .output1(_20_23_output1), .en(_20_23write), .output_select2(_20_23op2), .out_10(_20_23_out_10));
  GRF_reg _24_27 (
    .write_in(WD), .write_in_select(_24_27write_slt), .output_select1(_24_27op1), .reset(reset), .clk(clk),
    .WE(WE), .output1(_24_27_output1), .en(_24_27write), .output_select2(_24_27op2), .out_10(_24_27_out_10));
  GRF_reg _28_31 (
    .write_in(WD), .write_in_select(_28_31write_slt), .output_select1(_28_31op1), .reset(reset), .clk(clk),
    .WE(WE), .output1(_28_31_output1), .en(_28_31write), .output_select2(_28_31op2), .out_10(_28_31_out_10));
  Multiplexer #(.select(3), .width(32)) multiplexer_1 (
    .in0(_0_3_output1), .in1(_4_7_output1), .in2(_8_11_output1), .in3(_12_15_output1), .in4(_16_19_output1),
    .in5(_20_23_output1), .in6(_24_27_output1), .in7(_28_31_output1), .out(RD1), .sel(A1_output_slt[4:2]));  // open: en
  Multiplexer #(.select(3), .width(32)) multiplexer_2 (
    .in0(_0_3_output2), .in1(_4_7_out_10), .in2(_8_11_out_10), .in3(_12_15_out_10), .in4(_16_19_out_10),
    .in5(_20_23_out_10), .in6(_24_27_out_10), .in7(_28_31_out_10), .out(RD2), .sel(A2_output_slt[4:2]));  // open: en

  // Other names for the same wires on the sheet: select1[2:0] = A1_output_slt[4:2]; select2[2:0] = A2_output_slt[4:2]
endmodule

module GRF_reg0_3 (
  input  [31:0] write_in,
  input  [1:0] write_in_select,
  input  en,
  input  [1:0] output_select1,
  input  reset,
  input  clk,
  input  WE,
  input  [1:0] output_select2,
  output [31:0] output1,
  output [31:0] output2
);

  wire decoder_1_out1, decoder_1_out2, decoder_1_out3;
  wire [31:0] _0_q, _1_q, _2_q, _3_q, demultiplexer_1_out1, demultiplexer_1_out2, demultiplexer_1_out3,
       multiplexer_1_out, multiplexer_2_out, multiplexer_3_out;

  Demultiplexer #(.select(2), .width(32)) demultiplexer_1 (
    .out1(demultiplexer_1_out1), .out2(demultiplexer_1_out2), .out3(demultiplexer_1_out3), .in(write_in),
    .sel(write_in_select));  // open: out0, en
  Decoder #(.select(2), .disabled(0)) decoder_1 (
    .out1(decoder_1_out1), .out2(decoder_1_out2), .out3(decoder_1_out3), .sel(write_in_select), .en(en));  // open: out0
  Multiplexer #(.width(32)) multiplexer_1 (
    .in0(_1_q), .in1(demultiplexer_1_out1), .out(multiplexer_1_out), .sel(decoder_1_out1));  // open: en
  Multiplexer #(.width(32)) multiplexer_2 (
    .in0(_2_q), .in1(demultiplexer_1_out2), .out(multiplexer_2_out), .sel(decoder_1_out2));  // open: en
  Multiplexer #(.width(32)) multiplexer_3 (
    .in0(_3_q), .in1(demultiplexer_1_out3), .out(multiplexer_3_out), .sel(decoder_1_out3));  // open: en
  Register #(.width(32)) _0 (.D({32{1'b0}}), .en(WE), .Q(_0_q), .clk(clk), .clr(reset));
  Register #(.width(32)) _1 (.D(multiplexer_1_out), .en(WE), .Q(_1_q), .clk(clk), .clr(reset));
  Register #(.width(32)) _2 (.D(multiplexer_2_out), .en(WE), .Q(_2_q), .clk(clk), .clr(reset));
  Register #(.width(32)) _3 (.D(multiplexer_3_out), .en(WE), .Q(_3_q), .clk(clk), .clr(reset));
  Multiplexer #(.select(2), .width(32)) multiplexer_4 (
    .in0(_0_q), .in1(_1_q), .in2(_2_q), .in3(_3_q), .out(output1), .sel(output_select1));  // open: en
  Multiplexer #(.select(2), .width(32)) multiplexer_5 (
    .in0(_0_q), .in1(_1_q), .in2(_2_q), .in3(_3_q), .out(output2), .sel(output_select2));  // open: en
endmodule

// output2
module GRF_reg (
  input  [31:0] write_in,
  input  [1:0] write_in_select,
  input  en,
  input  [1:0] output_select1,
  input  [1:0] output_select2,
  input  reset,
  input  clk,
  input  WE,
  output [31:0] output1,
  output [31:0] out_10
);

  wire decoder_1_out0, decoder_1_out1, decoder_1_out2, decoder_1_out3;
  wire [31:0] _0_q, _1_q, _2_q, _3_q, demultiplexer_1_out0, demultiplexer_1_out1, demultiplexer_1_out2,
       demultiplexer_1_out3, multiplexer_1_out, multiplexer_2_out, multiplexer_3_out, multiplexer_4_out;

  Demultiplexer #(.select(2), .width(32)) demultiplexer_1 (
    .out0(demultiplexer_1_out0), .out1(demultiplexer_1_out1), .out2(demultiplexer_1_out2),
    .out3(demultiplexer_1_out3), .in(write_in), .sel(write_in_select));  // open: en
  Decoder #(.select(2), .disabled(0)) decoder_1 (
    .out0(decoder_1_out0), .out1(decoder_1_out1), .out2(decoder_1_out2), .out3(decoder_1_out3),
    .sel(write_in_select), .en(en));
  Multiplexer #(.width(32)) multiplexer_1 (
    .in0(_0_q), .in1(demultiplexer_1_out0), .out(multiplexer_1_out), .sel(decoder_1_out0));  // open: en
  Multiplexer #(.width(32)) multiplexer_2 (
    .in0(_1_q), .in1(demultiplexer_1_out1), .out(multiplexer_2_out), .sel(decoder_1_out1));  // open: en
  Multiplexer #(.width(32)) multiplexer_3 (
    .in0(_2_q), .in1(demultiplexer_1_out2), .out(multiplexer_3_out), .sel(decoder_1_out2));  // open: en
  Multiplexer #(.width(32)) multiplexer_4 (
    .in0(_3_q), .in1(demultiplexer_1_out3), .out(multiplexer_4_out), .sel(decoder_1_out3));  // open: en
  Register #(.width(32)) _0 (.D(multiplexer_1_out), .en(WE), .Q(_0_q), .clk(clk), .clr(reset));
  Register #(.width(32)) _1 (.D(multiplexer_2_out), .en(WE), .Q(_1_q), .clk(clk), .clr(reset));
  Register #(.width(32)) _2 (.D(multiplexer_3_out), .en(WE), .Q(_2_q), .clk(clk), .clr(reset));
  Register #(.width(32)) _3 (.D(multiplexer_4_out), .en(WE), .Q(_3_q), .clk(clk), .clr(reset));
  Multiplexer #(.select(2), .width(32)) multiplexer_5 (
    .in0(_0_q), .in1(_1_q), .in2(_2_q), .in3(_3_q), .out(output1), .sel(output_select1));  // open: en
  Multiplexer #(.select(2), .width(32)) multiplexer_6 (
    .in0(_0_q), .in1(_1_q), .in2(_2_q), .in3(_3_q), .out(out_10), .sel(output_select2));  // open: en
endmodule

module GRF_selector (
  input  [4:0] in_1,
  output [1:0] output_low2,
  output [2:0] output_high3
);


  assign output_high3 = in_1[4:2];
  assign output_low2 = in_1[1:0];
endmodule

module GRF_selector_2 (
  input  [4:0] in_1,
  output [1:0] out_2,
  output [1:0] out_3,
  output [1:0] out_4,
  output [1:0] out_5,
  output [1:0] out_6,
  output [1:0] out_7,
  output [1:0] out_8,
  output [1:0] out_9
);

  wire [1:0] grf_selector_1_output_low2;
  wire [2:0] grf_selector_1_output_high3;

  GRF_selector grf_selector_1 (
    .in_1(in_1), .output_low2(grf_selector_1_output_low2), .output_high3(grf_selector_1_output_high3));
  Demultiplexer #(.select(3), .width(2)) demultiplexer_1 (
    .out0(out_2), .out1(out_3), .out2(out_4), .out3(out_5), .out4(out_6), .out5(out_7), .out6(out_8),
    .out7(out_9), .in(grf_selector_1_output_low2), .sel(grf_selector_1_output_high3));  // open: en
endmodule

module GRF_text (
  input  WE,
  input  reset,
  input  clk,
  input  [4:0] A1,
  input  [4:0] A2,
  input  [4:0] A3,
  input  [31:0] in_7,
  output [31:0] out_8,
  output [31:0] out_9
);

  // GRF grf_1: pin names not known; wires that end beside it: A1, in_7, A2, A3, clk, reset, WE, out_8, out_9
endmodule

module NPC (
  input  [31:0] PC,
  input  [25:0] IMM,
  input  Zero,
  input  [31:0] RA,
  input  [2:0] NPCOp,
  output [31:0] PC_4,
  output [31:0] NPC
);

  wire [31:0] adder_2_out, bit_extender_1_out, multiplexer_1_out;

  assign bit_extender_1_out = {{14{IMM[15]}}, {IMM[15:0], 2'b00}};  // Bit_Extender bit_extender_1
  Adder #(.width(32)) adder_1 (.a(32'h4), .b(PC), .out(PC_4));  // open: cin, cout
  Adder #(.width(32)) adder_2 (.a(PC_4), .b(bit_extender_1_out), .out(adder_2_out));  // open: cin, cout
  Multiplexer #(.width(32)) multiplexer_1 (
    .in0(PC_4), .in1(adder_2_out), .out(multiplexer_1_out), .sel(Zero));  // open: en
  Multiplexer #(.select(3), .width(32)) multiplexer_2 (
    .in0(PC_4), .in1(multiplexer_1_out), .in2({PC[31:28], IMM, 2'b00}), .in3(RA), .out(NPC), .sel(NPCOp));  // open: in4, in5, in6, in7, en

  // Notes on the sheet:
  //   j,jal
  //   jr,jalr
  //   beq
endmodule

module Controller (
  input  [5:0] opcode,
  input  [5:0] func,
  output sllOp,
  output DMWr,
  output [1:0] DMOp,
  output [2:0] NPCOp,
  output [1:0] WRA3Sel,
  output [1:0] WDSel,
  output EXTOp,
  output WE,
  output ALUBSel,
  output [2:0] ALUOp
);

  wire add_out, beq_out, j_out, jal_out, jalr_out, jr_out, lb_out, lui_out, lw_out, not_1_out, not_2_out,
       not_3_out, not_4_out, not_5_out, not_6_out, not_7_out, not_8_out, not_9_out, not_10_out, not_11_out,
       not_12_out, ori_out, sb_out, special_out, sub_out, sw_out;

  not not_1 (not_1_out, opcode[4]);
  not not_2 (not_2_out, opcode[5]);
  not not_3 (not_3_out, opcode[3]);
  not not_4 (not_4_out, opcode[2]);
  not not_5 (not_5_out, opcode[1]);
  not not_6 (not_6_out, opcode[0]);
  not not_7 (not_7_out, func[5]);
  not not_8 (not_8_out, func[4]);
  not not_9 (not_9_out, func[3]);
  not not_10 (not_10_out, func[2]);
  not not_11 (not_11_out, func[1]);
  not not_12 (not_12_out, func[0]);
  and special (special_out, not_2_out, not_1_out, not_3_out, not_4_out, not_5_out, not_6_out);
  and add (add_out, func[5], not_8_out, not_9_out, special_out, not_10_out, not_11_out, not_12_out);
  and sub (sub_out, func[5], not_8_out, not_9_out, special_out, not_10_out, func[1], not_12_out);
  and ori (ori_out, not_2_out, not_1_out, opcode[3], opcode[2], not_5_out, opcode[0]);
  and lw (lw_out, opcode[5], not_1_out, not_3_out, not_4_out, opcode[1], opcode[0]);
  and sw (sw_out, opcode[5], not_1_out, opcode[3], not_4_out, opcode[1], opcode[0]);
  and beq (beq_out, not_2_out, not_1_out, not_3_out, opcode[2], not_5_out, not_6_out);
  and sll (sllOp, not_7_out, not_8_out, not_9_out, special_out, not_10_out, not_11_out, not_12_out);
  and lui (lui_out, not_2_out, not_1_out, opcode[3], opcode[2], opcode[1], opcode[0]);
  and j (j_out, not_2_out, not_1_out, not_3_out, not_4_out, opcode[1], not_6_out);
  and jal (jal_out, not_2_out, not_1_out, not_3_out, not_4_out, opcode[1], opcode[0]);
  and jr (jr_out, not_7_out, not_8_out, func[3], special_out, not_10_out, not_11_out, not_12_out);
  and jalr (jalr_out, not_7_out, not_8_out, func[3], special_out, not_10_out, not_11_out, func[0]);
  and lb (lb_out, opcode[5], not_1_out, not_3_out, not_4_out, not_5_out, not_6_out);
  and sb (sb_out, opcode[5], not_1_out, opcode[3], not_4_out, not_5_out, not_6_out);
  or WRA3Sel_1 (WRA3Sel[1], jal_out, 1'b0);
  or WRA3Sel_0 (WRA3Sel[0], sb_out, ori_out, lw_out, sw_out, lui_out, 1'b0, lb_out);
  or WDSel_1 (WDSel[1], jal_out, jalr_out, 1'b0);
  or WDSel_0 (WDSel[0], add_out, sub_out, ori_out, lui_out, 1'b0, sllOp);
  or or_1 (EXTOp, lw_out, sw_out, lb_out, sb_out, 1'b0);
  or or_2 (WE, jalr_out, sllOp, add_out, sub_out, ori_out, lw_out, 1'b0, lui_out, jal_out, lb_out);
  or or_3 (ALUBSel, lb_out, ori_out, lw_out, sw_out, sllOp, 1'b0, lui_out, sb_out);
  or ALUOp_2 (ALUOp[2], lui_out, 1'b0);
  or ALUOp_1 (ALUOp[1], ori_out, sllOp, 1'b0);
  or ALUOp_0 (ALUOp[0], sub_out, beq_out, sllOp, 1'b0);
  or ALUOp_0_2 (DMWr, sw_out, sb_out, 1'b0);
  buf ALUOp_0_3 (DMOp[1], 1'b0);  // OR_Gate
  or ALUOp_0_4 (DMOp[0], lb_out, sb_out, 1'b0);
  buf NPCOp_1 (NPCOp[2], 1'b0);  // OR_Gate
  or NPCOp_1_2 (NPCOp[1], j_out, jal_out, jr_out, jalr_out, 1'b0);
  or NPCOp_0 (NPCOp[0], beq_out, jr_out, jalr_out, 1'b0);

  // Notes on the sheet:
  //   opcode[5]
  //   opcode[4]
  //   opcode[3]
  //   opcode[2]
  //   opcode[1]
  //   opcode[0]
  //   func[0]
  //   001101
  //   100011
  //   101011
  //   000100
endmodule

module ALU (
  input  [31:0] A,
  input  [31:0] B,
  input  [2:0] in_3,
  output [31:0] out_4,
  output Zero,
  output LessZero
);

  wire [31:0] adder_1_out, or_1_out, shifter_1_out, subtractor_1_out;

  Comparator #(.width(32)) comparator_1 (.a(A), .b(B), .eq(Zero), .lt(LessZero));  // open: gt
  Adder #(.width(32)) adder_1 (.a(A), .b(B), .out(adder_1_out));  // open: cin, cout
  Subtractor #(.width(32)) subtractor_1 (.a(A), .b(B), .out(subtractor_1_out));  // open: bin, bout
  assign or_1_out = A | B;  // OR_Gate or_1, 32 bits wide
  Shifter #(.width(32)) shifter_1 (.in(A), .\dist (B[10:6]), .out(shifter_1_out));
  Multiplexer #(.select(3), .width(32)) multiplexer_1 (
    .in0(adder_1_out), .in1(subtractor_1_out), .in2(or_1_out), .in3(shifter_1_out),
    .in4({B[15:0], {16{1'b0}}}), .out(out_4), .sel(in_3));  // open: in5, in6, in7, en
endmodule

module DM (
  input  [31:0] Addr,
  input  [31:0] WD,
  input  [1:0] DMOp,
  input  clk,
  input  reset,
  input  DMWr,
  output [31:0] out_7,
  output [31:0] RD
);

  wire [7:0] multiplexer_3_out, RD_7__0, RD_15__8, RD_23__16, RD_31__24;
  wire [31:0] bit_extender_1_out, multiplexer_1_out;

  Multiplexer #(.select(2), .width(32)) multiplexer_1 (
    .in0({RD_31__24, RD_23__16, RD_15__8, WD[7:0]}), .in1({RD_31__24, RD_23__16, WD[7:0], RD_7__0}),
    .in2({RD_31__24, WD[7:0], RD_15__8, RD_7__0}), .in3({WD[7:0], RD_23__16, RD_15__8, RD_7__0}),
    .out(multiplexer_1_out), .sel(Addr[1:0]));  // open: en
  Multiplexer #(.select(2), .width(32)) multiplexer_2 (
    .in0(WD), .in1(multiplexer_1_out), .out(out_7), .sel(DMOp));  // open: in2, in3, en
  RAM #(.addrWidth(16), .dataWidth(32), .bus("separate")) ram_1 (
    .addr(Addr[17:2]), .din(out_7), .data({RD_31__24, RD_23__16, RD_15__8, RD_7__0}), .str(DMWr), .clk(clk),
    .clr(reset));  // open: sel, ld
  Multiplexer #(.select(2), .width(8)) multiplexer_3 (
    .in0(RD_7__0), .in1(RD_15__8), .in2(RD_23__16), .in3(RD_31__24), .out(multiplexer_3_out), .sel(Addr[1:0]));  // open: en
  assign bit_extender_1_out = {{24{multiplexer_3_out[7]}}, multiplexer_3_out};  // Bit_Extender bit_extender_1
  Multiplexer #(.select(2), .width(32)) multiplexer_4 (
    .in0({RD_31__24, RD_23__16, RD_15__8, RD_7__0}), .in1(bit_extender_1_out), .out(RD), .sel(DMOp));  // open: in2, in3, en

  // Other names for the same wires on the sheet: WD_15__8[7:0] = WD[15:8]; WD_23__16[7:0] = WD[23:16];
  //   WD_31__24[7:0] = WD[31:24]; WD_7__0[7:0] = WD[7:0]; address[1:0] = Addr[1:0]; WD_t[31:0] = out_7; Wr = DMWr
endmodule

module Ext (
  input  EXTOp,
  input  [15:0] IMM_15_0,
  output [31:0] extend
);

  wire [31:0] bit_extender_1_out, bit_extender_2_out;

  assign bit_extender_1_out = {{16{1'b0}}, IMM_15_0};  // Bit_Extender bit_extender_1
  assign bit_extender_2_out = {{16{IMM_15_0[15]}}, IMM_15_0};  // Bit_Extender bit_extender_2
  Multiplexer #(.width(32)) multiplexer_1 (
    .in0(bit_extender_1_out), .in1(bit_extender_2_out), .out(extend), .sel(EXTOp));  // open: en
endmodule

module R_Logic (
  input  func_5,
  input  func_4,
  input  func_3,
  input  func_2,
  input  func_1,
  input  func_0,
  output add,
  output sub,
  output sll
);

  wire not_1_out, not_2_out, not_3_out, not_4_out, not_5_out, not_6_out, not_7_out, not_8_out, not_9_out,
       not_10_out, not_11_out, not_12_out, not_13_out, not_14_out, not_15_out;

  not not_1 (not_1_out, func_4);
  not not_2 (not_2_out, func_3);
  not not_3 (not_3_out, func_2);
  not not_4 (not_4_out, func_1);
  not not_5 (not_5_out, func_0);
  not not_6 (not_6_out, func_4);
  not not_7 (not_7_out, func_3);
  not not_8 (not_8_out, func_2);
  not not_9 (not_9_out, func_0);
  not not_10 (not_10_out, func_5);
  not not_11 (not_11_out, func_4);
  not not_12 (not_12_out, func_3);
  not not_13 (not_13_out, func_2);
  not not_14 (not_14_out, func_1);
  not not_15 (not_15_out, func_0);
  and and_1 (add, func_5, not_1_out, not_2_out, not_3_out, not_4_out, not_5_out);
  and and_2 (sub, func_5, not_6_out, not_7_out, not_8_out, func_1, not_9_out);
  and and_3 (sll, not_10_out, not_11_out, not_12_out, not_13_out, not_14_out, not_15_out);
endmodule

module PC (
  input  [31:0] NPC,
  input  clk,
  input  reset,
  output [15:0] out_4,
  output [31:0] PC
);

  wire [31:0] subtractor_1_out;

  Subtractor #(.width(32)) subtractor_1 (.a(NPC), .b(32'h3000), .out(subtractor_1_out));  // open: bin, bout
  Register #(.width(16)) register_1 (.D(subtractor_1_out[17:2]), .Q(out_4), .clk(clk), .clr(reset));  // open: en
  Adder #(.width(32)) adder_1 (.a({{14{1'b0}}, out_4, 2'b00}), .b(32'h3000), .out(PC));  // open: cin, cout
endmodule
