// Logisim project 4BitSort.circ as structural Verilog: 3 circuits, main circuit 1bit_swap
module _1bit_swap (
  input  A,
  input  B,
  input  S,
  output _1,
  output _2
);

  wire and_1_out, and_2_out, and_3_out, and_4_out, not_1_out;

  not not_1 (not_1_out, S);
  and and_1 (and_1_out, S, A);
  and and_2 (and_2_out, not_1_out, A);
  and and_3 (and_3_out, S, B);
  and and_4 (and_4_out, B, not_1_out);
  or or_1 (_1, and_2_out, and_3_out);
  or or_2 (_2, and_1_out, and_4_out);
endmodule

module _4bit_swap (
  input  [3:0] in_1,
  input  [3:0] in_2,
  input  in_3,
  output [3:0] out_4,
  output [3:0] out_5
);

  _1bit_swap u_1bit_swap_1 (.A(in_1[0]), .B(in_2[0]), .S(in_3), ._1(out_4[0]), ._2(out_5[0]));
  _1bit_swap u_1bit_swap_2 (.A(in_1[1]), .B(in_2[1]), .S(in_3), ._1(out_4[1]), ._2(out_5[1]));
  _1bit_swap u_1bit_swap_3 (.A(in_1[2]), .B(in_2[2]), .S(in_3), ._1(out_4[2]), ._2(out_5[2]));
  _1bit_swap u_1bit_swap_4 (.A(in_1[3]), .B(in_2[3]), .S(in_3), ._1(out_4[3]), ._2(out_5[3]));
endmodule

module _4bit_sort (
  input  [3:0] A,
  input  [3:0] B,
  input  [3:0] C,
  input  [3:0] D,
  output [3:0] _1,
  output [3:0] _2,
  output [3:0] _3,
  output [3:0] _4
);

  wire comparator_1_lt, comparator_2_lt, comparator_3_lt, comparator_4_lt, comparator_5_lt, comparator_6_lt;
  wire [3:0] n4bit_swap_1_out_4, n4bit_swap_1_out_5, n4bit_swap_2_out_4, n4bit_swap_2_out_5,
       n4bit_swap_3_out_4, n4bit_swap_3_out_5, n4bit_swap_4_out_5, n4bit_swap_5_out_4;

  Comparator #(.width(4)) comparator_1 (.a(A), .b(B), .lt(comparator_1_lt));  // open: gt, eq
  _4bit_swap u_4bit_swap_1 (
    .in_1(A), .in_2(B), .in_3(comparator_1_lt), .out_4(n4bit_swap_1_out_4), .out_5(n4bit_swap_1_out_5));
  // Probe on n4bit_swap_1_out_4
  // Probe on D
  Comparator #(.width(4), .mode("unsigned")) comparator_2 (
    .a(n4bit_swap_1_out_5), .b(C), .lt(comparator_2_lt));  // open: gt, eq
  Comparator #(.width(4), .mode("unsigned")) comparator_3 (
    .a(n4bit_swap_1_out_4), .b(D), .lt(comparator_3_lt));  // open: gt, eq
  _4bit_swap u_4bit_swap_2 (
    .in_1(n4bit_swap_1_out_5), .in_2(C), .in_3(comparator_2_lt), .out_4(n4bit_swap_2_out_4),
    .out_5(n4bit_swap_2_out_5));
  _4bit_swap u_4bit_swap_3 (
    .in_1(n4bit_swap_1_out_4), .in_2(D), .in_3(comparator_3_lt), .out_4(n4bit_swap_3_out_4),
    .out_5(n4bit_swap_3_out_5));
  Comparator #(.width(4), .mode("unsigned")) comparator_4 (
    .a(n4bit_swap_2_out_4), .b(n4bit_swap_3_out_4), .lt(comparator_4_lt));  // open: gt, eq
  Comparator #(.width(4), .mode("unsigned")) comparator_5 (
    .a(n4bit_swap_2_out_5), .b(n4bit_swap_3_out_5), .lt(comparator_5_lt));  // open: gt, eq
  _4bit_swap u_4bit_swap_4 (
    .in_1(n4bit_swap_2_out_4), .in_2(n4bit_swap_3_out_4), .in_3(comparator_4_lt), .out_4(_4),
    .out_5(n4bit_swap_4_out_5));
  _4bit_swap u_4bit_swap_5 (
    .in_1(n4bit_swap_2_out_5), .in_2(n4bit_swap_3_out_5), .in_3(comparator_5_lt), .out_4(n4bit_swap_5_out_4),
    .out_5(_1));
  Comparator #(.width(4), .mode("unsigned")) comparator_6 (
    .a(n4bit_swap_4_out_5), .b(n4bit_swap_5_out_4), .lt(comparator_6_lt));  // open: gt, eq
  _4bit_swap u_4bit_swap_6 (
    .in_1(n4bit_swap_4_out_5), .in_2(n4bit_swap_5_out_4), .in_3(comparator_6_lt), .out_4(_3), .out_5(_2));

  // Notes on the sheet:
  //   up is larger
  //   ABD most large
endmodule
