// Logisim project Logisim_fibonacci_1 .circ as structural Verilog: 3 circuits, main circuit main
module main (
  input  [2:0] in_1,
  output [3:0] out_2
);

  wire output_time;
  wire [3:0] \output ;

  // Probe on output_time
  // Probe on output_time
  \计数  \u_计数  (.in_1(in_1), .out_2(output_time));
  \计算  \u_计算  (.in_1(output_time), .out_2(\output ));
  // Probe on \output 
  Multiplexer #(.width(4)) multiplexer_1 (.in0(4'b0000), .in1(\output ), .out(out_2), .sel(output_time));  // open: en
  // Probe on out_2
endmodule

module \计数  (
  input  [2:0] in_1,
  output out_2
);

  wire clock_1_out;
  wire [3:0] bit_extender_1_out, time_have_gone;

  assign bit_extender_1_out = {{1{1'b0}}, in_1};  // Bit_Extender bit_extender_1
  Clock clock_1 (.out(clock_1_out));
  Counter #(.width(4), .max('h8), .ongoal("stay")) counter_1 (
    .Q(time_have_gone), .clk(clock_1_out));  // open: load, D, count, carry, clr
  // Probe on time_have_gone
  Comparator #(.width(4), .mode("unsigned")) comparator_1 (
    .a(bit_extender_1_out), .b(time_have_gone), .lt(out_2));  // open: gt, eq
endmodule

module \计算  (
  input  in_1,
  output [3:0] out_2
);

  wire \begin , clock_1_out, clock_2_out, enable;
  wire [3:0] adder_1_out, multiplexer_1_out, prev_q;

  Clock clock_1 (.out(clock_1_out));
  Multiplexer #(.width(4)) multiplexer_1 (
    .in0(4'b0001), .in1(out_2), .out(multiplexer_1_out), .sel(\begin ));  // open: en
  Clock clock_2 (.out(clock_2_out));
  not not_1 (enable, in_1);
  Counter #(.width(1), .max('h1), .ongoal("stay")) counter_1 (
    .Q(\begin ), .clk(clock_1_out));  // open: load, D, count, carry, clr
  Register #(.width(4)) now (.D(adder_1_out), .en(enable), .Q(out_2), .clk(clock_2_out));  // open: clr
  Register #(.width(4)) prev (.D(multiplexer_1_out), .en(enable), .Q(prev_q), .clk(clock_2_out));  // open: clr
  Adder #(.width(4)) adder_1 (.a(out_2), .b(prev_q), .out(adder_1_out));  // open: cin, cout
  // Probe on adder_1_out

  // Other names for the same wires on the sheet: now[3:0] = out_2
endmodule
