// Logisim project mod5.circ as structural Verilog: 1 circuit, main circuit mod5
module mod5 (
  input  in_1,
  output out_2,
  output out_3,
  output out_4,
  output out_5,
  output out_6
);

  wire and_1_out, and_2_out, and_3_out, and_4_out, clock_1_out, not_1_out, not_2_out, not_3_out, not_4_out,
       not_5_out, not_6_out, not_7_out, register_1_q, register_2_q, xnor_1_out, xor_1_out, xor_2_out,
       xor_3_out;

  ExactlyOne xor_1 (.out(xor_1_out), .in0(in_1), .in2(register_1_q), .in4(register_2_q));
  xnor xnor_1 (xnor_1_out, register_1_q, register_2_q);
  Clock clock_1 (.out(clock_1_out));
  Register #(.width(1)) register_1 (.D(xor_1_out), .Q(register_1_q), .clk(clock_1_out));  // open: en, clr
  Register #(.width(1)) register_2 (.D(xnor_1_out), .Q(register_2_q), .clk(clock_1_out));  // open: en, clr
  not not_1 (not_1_out, in_1);
  not not_2 (not_2_out, register_1_q);
  not not_3 (not_3_out, register_2_q);
  not not_4 (not_4_out, in_1);
  not not_5 (not_5_out, register_2_q);
  not not_6 (not_6_out, register_1_q);
  xor xor_2 (xor_2_out, register_2_q, register_1_q);
  xor xor_3 (xor_3_out, register_1_q, register_2_q);
  not not_7 (not_7_out, in_1);
  and and_1 (and_1_out, not_1_out, not_2_out, not_3_out);
  and and_2 (and_2_out, not_4_out, register_2_q, register_1_q);
  and and_3 (and_3_out, in_1, register_2_q, register_1_q);
  and and_4 (and_4_out, in_1, not_5_out, not_6_out);
  or or_1 (out_3, and_1_out, and_2_out);
  or or_2 (out_4, and_3_out, and_4_out);
  and and_5 (out_5, xor_2_out, in_1);
  and and_6 (out_6, xor_3_out, not_7_out);

  assign out_2 = 1'b0;

  // Notes on the sheet:
  //   C0
  //   C1
endmodule
